# Fritzing sketch ESP8266_PIR (saved by Fritzing 0.9.3b)
breadboards: 1

parts:
  U1 = NodeMCU V3.0
  J1 = Infrared Proximity Sensor
  R2 = PHOTOCELL [package=photocell]
  R3 = Resistor [tolerance=±5% resistance=220 package=THT]
  R4 = Resistor [tolerance=±5% resistance=220 package=THT]

nets:
  3V3: U1.3V3, J1.Vcc, R3.Pin_1
  N1: U1.GND#6, U1.GND#13, U1.GND#16, U1.GND#33, R2.P$1, R4.Pin_1
  N2: U1.D7, J1.Vout
  N3: U1.A0, R2.P$2, R3.Pin_0
  N4: J1.GND, R4.Pin_0

custom parts:
  NodeMCU V3.0: ESP8266 based NodeMCU
